# Fritzing sketch SSG_FAL_M0-v20240719 (saved by Fritzing 0.9.10b)

parts:
  Part16 = Adafruit Feather M0 Adalogger [part_number="Adafruit #2796"]
  BAT1 = Battery Holders [package=lipo-1100mAh]  # not connected
  Part18 = Adafruit DS3231 STEMMA QT [part_number="Adafruit #5188"]
  Part19 = OLED Monochrome 128x64 0.96 inch [part_number=326]  # not connected
  DS5 = DS18B20 1-Wire Temperature Sensor [part_number=DS18B20]
  R19 = Resistor [tolerance=±5% resistance=4.7k power=0.25 package=THT]

nets:
  GND: Part16.GND, Part16.D12, Part18.GND, DS5.GND
  N1: Part16.A2, DS5.DQ, R19.Pin_0
  +3V3: Part16.+3V3, Part18.VCC, DS5.VDD, R19.Pin_1
  N2: Part16.SCL, Part18.SCL
  N3: Part16.SDA, Part18.SDA

notes:
  SSG_FAL_MO
  Snow & Stream Gauge Feather AdaLogger M0 Schematic v2024-07-19
  Sensors Supported
  BMP280,BME280,BMP3XX
  MCP9808
  Dallas 1-Wite 18B20
  Adafruit OLED 128x32
  Display SSD1306
  I2C 7-bit address 0x3C
  Feather SD
  Pin - D4 SD CS
  Pin - SPI MOSI
  Pin - SPI MISO
  Pin - SPI CLK
  Console Enable Jumper
  Jump Pin 12 to Ground
  Snow & Stream Gauge A3
  Adafruit DS3231
  RTC
  I2C 7-bit address 0x68
  DS18B20 Onewire Temperature
  Pin 1 GND
  Pin 2 DATA
  Pin 3 3.3V

custom parts:
  Adafruit Feather M0 Adalogger: This is the Adafruit Feather M0 Adalogger - our take on an 'all-in-one' Cortex M0 datalogger (or data-reader) with built in USB and battery charging. Its an Adafruit Feather M0 with a microSD holder ready to rock! We have other boards in the Feather family, check'em out here At the Feather M0's heart is an ATSAMD21G18 ARM Cortex M0 processor, clocked at 48 MHz and at 3.3V logic, the same one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
  Adafruit DS3231 STEMMA QT: The datasheet for the DS3231 explains that this part is an "Extremely Accurate I²C-Integrated RTC/TCXO/Crystal". And, hey, it does exactly what it says on the tin! This Real Time Clock (RTC) is the most precise you can get in a small, low-power package. We've had a breakout board version of this RTC for a while, but we want to make it even easier for folks to use, so now it comes with STEMMA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
  OLED Monochrome 128x64 0.96 inch: These displays are small, only about 1" diameter, but very readable due to the high contrast of an OLED display. This display is made of 128x64 individual white OLED pixels, each one is turned on or off by the controller chip. Because the display makes its own light, no backlight is required. This reduces the power required to run the OLED and is why the display has such high contrast; we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
